# Fritzing sketch Untitled Sketch 2 (saved by Fritzing 0.9.3b)
breadboards: 1

parts:
  Part1 = Arduino Uno (Rev3)
  S1 = H-Bridge with L298N
  M1 = Getriebemotor
  M2 = Getriebemotor
  M3 = Getriebemotor
  M4 = Getriebemotor
  VCC1 = Battery block 9V  # not connected
  VCC2 = Battery block 9V
  hc-sr1 = hc-sr04
  M5 = MH Sensor Series 4-pin IR Sensor/Line follower [package=THT]
  M6 = MH Sensor Series 4-pin IR Sensor/Line follower [package=THT]
  J1 = Basic Servo

nets:
  N1: Part1.A0, M6.pin1
  N2: Part1.A1, M5.pin1
  N3: Part1.D8, S1.IN2
  N4: Part1.D9_PWM, S1.IN1
  N5: Part1.D10_PWM/SS, S1.ENA
  N6: Part1.D11_PWM/MOSI, J1.pulse
  N7: Part1.D2, hc-sr1.Trig
  N8: Part1.D3_PWM, hc-sr1.Echo
  N9: Part1.D5_PWM, S1.ENB
  N10: Part1.D6_PWM, S1.IN4
  N11: Part1.D7, S1.IN3
  GND: Part1.GND, S1.GND, VCC2.-
  N12: S1.12V, VCC2.+
  N13: S1.M1-01, M3.pin_1
  N14: S1.M1-02, M3.pin_2, M4.pin_1
  N15: S1.M2-01, M1.pin_1, M2.pin_2
  N16: S1.M2-02, M1.pin_2, M2.pin_1
  N17: hc-sr1.VCC, M6.pin4
  N18: hc-sr1.GND, M6.pin3

custom parts:
  H-Bridge with L298N: h-bridge
  MH Sensor Series 4-pin IR Sensor/Line follower: modified version of FC-51 from Peter Van Epp (vanepp in forums) This is the 4-pin version of IR line follower module, using the TCRT5000 sensor and LM393 comparator This one has the analogue output pin, in addition to the Digital pin which is set by the trimmer. The Analog pin can feed an Arduino ADC input, for much better level sensing options and less drift than the crappy potentiometer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
